# Fritzing sketch RFB6_connect (saved by Fritzing 0.9.3b)
breadboards: 1

parts:
  WeMos_D1_Mini1 = WeMos D1 Mini  # not connected
  RXB6 = RF-LINK_RX [part_number=RXB6 package=rf-link_rx]
  ANT1 = Antenna

nets:
  N1: RXB6.GND, ANT1.antenna_lead
