# Fritzing sketch RXB6_connect (saved by Fritzing 0.9.3b)
circuit board: 4.7501cm x 4.6238cm
breadboards: 1

parts:
  WeMos_D1_Mini1 = WeMos D1 Mini
  ANT1 = Antenna
  U1 = RXB6 [part_number=RXB6 package=rf-link_rx]

nets:
  N1: WeMos_D1_Mini1.3V3, U1.VCC#5
  N2: WeMos_D1_Mini1.G, U1.GND#8
  N3: ANT1.antenna_lead, U1.Antena

custom parts:
  RXB6: RF Link receivers- WRL-8947, 8948, 8949, 8950
