# Fritzing sketch W132_connect (saved by Fritzing 0.9.3b)
breadboards: 1

parts:
  WeMos_D1_Mini1 = WeMos D1 Mini
  Venus_W1 = Venus W132

nets:
  3V3: WeMos_D1_Mini1.3V3, Venus_W1.VCC
  N1: WeMos_D1_Mini1.G, Venus_W1.GND

custom parts:
  Venus W132: Venus W132 anemometer
